// Logisim project tabla transiciones.circ as structural Verilog
module EECC (
  input  a,
  input  b,
  input  c,
  output add1,
  output op1_A,
  output op2_B,
  output cpl
);

  wire and_1_out, and_2_out, not_1_out, not_2_out, not_3_out, not_4_out;

  or or_1 (add1, c, a);
  not not_1 (not_1_out, c);
  not not_2 (not_2_out, c);
  not not_3 (not_3_out, a);
  not not_4 (not_4_out, b);
  and and_1 (and_1_out, b, not_1_out);
  and and_2 (and_2_out, b, not_2_out);
  and and_3 (cpl, not_3_out, not_4_out, c);
  or or_2 (op1_A, a, and_1_out);
  or or_3 (op2_B, a, and_2_out);
endmodule
